// Logisim project ex5.circ as structural Verilog: 1 circuit, main circuit num_checker
module num_checker (
  input  [31:0] num,
  input  clk,
  output is_odd,
  output is_even,
  output is_zero,
  output greater_than_sixteen,
  output five_or_ten
);

  wire comparator_5_eq, comparator_6_eq;
  wire [7:0] register_1_q, undriven;

  Register register_1 (.D(undriven), .clk(clk), .Q(register_1_q));  // open: en, clr
  Adder adder_1 (.a(register_1_q), .b(8'h1));  // open: out, cin, cout
  Comparator #(.width(1)) comparator_1 (.a(num[0]), .b(1'b1), .eq(is_odd));  // open: gt, lt
  Comparator #(.width(1)) comparator_2 (.a(num[0]), .b(1'b0), .eq(is_even));  // open: gt, lt
  Comparator #(.width(32)) comparator_3 (.a(num), .b({32{1'b0}}), .eq(is_zero));  // open: gt, lt
  Comparator #(.width(28)) comparator_4 (.a(num[31:4]), .b({28{1'b0}}), .gt(greater_than_sixteen));  // open: eq, lt
  Comparator #(.width(32)) comparator_5 (.a(num), .b(32'h5), .eq(comparator_5_eq));  // open: gt, lt
  Comparator #(.width(32)) comparator_6 (.a(num), .b(32'ha), .eq(comparator_6_eq));  // open: gt, lt
  or or_1 (five_or_ten, comparator_5_eq, comparator_6_eq);

  // Other names for the same wires on the sheet: bit_zero = num[0]; bits_five[2:0] = num[2:0];
  //   ten_rest_zero[29:0] = {num[31:4], num[2], num[0]}; bits_ten[1:0] = {num[3], num[1]};
  //   five_rest_zero[28:0] = num[31:3]; bits_16[27:0] = num[31:4]
endmodule
