// Logisim project branch-comp.circ as structural Verilog: 1 circuit, main circuit branch_comp
module branch_comp (
  input  [31:0] BrData1,
  input  [31:0] BrData2,
  input  BrUn,
  output BrEq,
  output BrLt
);

  wire BrEqS, BrEqU, BrLtS, BrLtU;

  Comparator #(.mode("unsigned"), .width(32)) comparator_1 (
    .a(BrData1), .b(BrData2), .eq(BrEqU), .lt(BrLtU));  // open: gt
  Comparator #(.width(32)) comparator_2 (.a(BrData1), .b(BrData2), .eq(BrEqS), .lt(BrLtS));  // open: gt
  Multiplexer multiplexer_1 (.in0(BrEqS), .in1(BrEqU), .out(BrEq), .sel(BrUn));
  Multiplexer multiplexer_2 (.in0(BrLtS), .in1(BrLtU), .out(BrLt), .sel(BrUn));

  // Notes on the sheet:
  //   INPUTS to your circuit
  //   How do you deal with the Signed/Unisigned?
  //   DON'T CHANGE THE LOCATIONS OF THE INPUTS AND OUTPUTS!
  //   OUTPUT from your circuit
endmodule
