// Logisim project control-logic.circ as structural Verilog: 1 circuit, main circuit control_logic
module control_logic (
  input  [31:0] Instruction,
  input  BrEq,
  input  BrLt,
  output PCSel,
  output RegWEn,
  output [2:0] ImmSel,
  output BrUn,
  output ASel,
  output BSel,
  output [3:0] ALUSel,
  output MemWEn,
  output [1:0] WBSel
);

  wire add, addi, aiupc, and0, and_21_out, and_22_out, and_23_out, and_24_out, and_28_out, and_29_out, andi,
       beq, bge, bgeu, blt, bltu, bne, BType, Func3_0, Func3_1, Func3_2, Func3_3, Func3_4, Func3_5, Func3_6,
       Func3_7, Func7_0, Func7_1, Func7_20, Itype, jal, jalr, lb, lh, Loads, lui, lw, mul, mulh, mulhu,
       not_1_out, not_2_out, not_3_out, or0, or_2_out, ori, Rtype, sb, sh, sll0, slli, slt, slti, sra0, srai,
       srl0, srli, Stores, sub, sw, xor0, xori;
  wire [5:0] RomInput;
  wire [15:14] rom_1_data;

  Comparator #(.width(3)) comparator_1 (.a(Instruction[14:12]), .b(3'b000), .eq(Func3_0));  // open: gt, lt
  Comparator #(.width(3)) comparator_2 (.a(Instruction[14:12]), .b(3'b010), .eq(Func3_2));  // open: gt, lt
  Comparator #(.width(3)) comparator_3 (.a(Instruction[14:12]), .b(3'b100), .eq(Func3_4));  // open: gt, lt
  Comparator #(.width(3)) comparator_4 (.a(Instruction[14:12]), .b(3'b110), .eq(Func3_6));  // open: gt, lt
  Comparator #(.width(7)) comparator_5 (.a(Instruction[31:25]), .b({7{1'b0}}), .eq(Func7_0));  // open: gt, lt
  Comparator #(.width(7)) comparator_6 (.a(Instruction[31:25]), .b(7'b0000001), .eq(Func7_1));  // open: gt, lt
  and and_1 (slt, Rtype, Func3_2, Func7_0);
  and and_2 (mul, Rtype, Func3_0, Func7_1);
  and and_3 (mulh, Rtype, Func3_1, Func7_1);
  and and_4 (mulhu, Rtype, Func3_3, Func7_1);
  ROM #(.addrWidth(6), .dataWidth(16)) rom_1 (
    .addr(RomInput), .data({rom_1_data, WBSel, MemWEn, ALUSel, BSel, ASel, BrUn, ImmSel, RegWEn}));
  Comparator #(.width(3)) comparator_7 (.a(Instruction[14:12]), .b(3'b001), .eq(Func3_1));  // open: gt, lt
  Comparator #(.width(3)) comparator_8 (.a(Instruction[14:12]), .b(3'b011), .eq(Func3_3));  // open: gt, lt
  Comparator #(.width(3)) comparator_9 (.a(Instruction[14:12]), .b(3'b101), .eq(Func3_5));  // open: gt, lt
  Comparator #(.width(3)) comparator_10 (.a(Instruction[14:12]), .b(3'b111), .eq(Func3_7));  // open: gt, lt
  Comparator #(.width(7)) comparator_11 (.a(Instruction[31:25]), .b(7'b0100000), .eq(Func7_20));  // open: gt, lt
  and and_5 (add, Rtype, Func3_0, Func7_0);
  and and_6 (sub, Rtype, Func3_0, Func7_20);
  and and_7 (and0, Rtype, Func3_7, Func7_0);
  and and_8 (or0, Rtype, Func3_6, Func7_0);
  Comparator #(.width(7)) comparator_12 (.a(Instruction[6:0]), .b(7'b0010011), .eq(Itype));  // open: gt, lt
  Comparator #(.width(7)) comparator_13 (.a(Instruction[6:0]), .b(7'b0110011), .eq(Rtype));  // open: gt, lt
  Comparator #(.width(7)) comparator_14 (.a(Instruction[6:0]), .b(7'b1100011), .eq(BType));  // open: gt, lt
  and and_9 (addi, Itype, Func3_0);
  and and_10 (andi, Itype, Func3_7);
  and and_11 (ori, Itype, Func3_6);
  and and_12 (xori, Itype, Func3_4);
  and and_13 (slti, Itype, Func3_2);
  and and_14 (xor0, Rtype, Func3_4, Func7_0);
  and and_15 (sll0, Rtype, Func3_1, Func7_0);
  and and_16 (srl0, Rtype, Func3_5, Func7_0);
  and and_17 (sra0, Rtype, Func3_5, Func7_20);
  Comparator #(.width(7)) comparator_15 (.a(Instruction[6:0]), .b(7'b0000011), .eq(Loads));  // open: gt, lt
  Comparator #(.width(7)) comparator_16 (.a(Instruction[6:0]), .b(7'b0100011), .eq(Stores));  // open: gt, lt
  Comparator #(.width(7)) comparator_17 (.a(Instruction[6:0]), .b(7'b1101111), .eq(jal));  // open: gt, lt
  Comparator #(.width(7)) comparator_18 (.a(Instruction[6:0]), .b(7'b1100111), .eq(jalr));  // open: gt, lt
  or or_1 (PCSel, and_21_out, and_22_out, and_28_out, or_2_out, and_23_out, and_29_out, and_24_out);
  and and_18 (slli, Itype, Func3_1, Func7_0);
  and and_19 (srli, Itype, Func3_5, Func7_0);
  and and_20 (srai, Itype, Func3_5, Func7_20);
  and and_21 (and_21_out, beq, BrEq);
  and and_22 (and_22_out, bne, not_1_out);
  and and_23 (and_23_out, BrLt, blt);
  and and_24 (and_24_out, BrLt, bltu);
  Comparator #(.width(7)) comparator_19 (.a(Instruction[6:0]), .b(7'b0010111), .eq(aiupc));  // open: gt, lt
  Comparator #(.width(7)) comparator_20 (.a(Instruction[6:0]), .b(7'b0110111), .eq(lui));  // open: gt, lt
  and and_25 (lb, Loads, Func3_0);
  and and_26 (lh, Loads, Func3_1);
  and and_27 (lw, Loads, Func3_2);
  not not_1 (not_1_out, BrEq);
  or or_2 (or_2_out, jal, jalr);
  and and_28 (and_28_out, bgeu, not_2_out);
  and and_29 (and_29_out, bge, not_3_out);
  and and_30 (beq, BType, Func3_0);
  and and_31 (bge, BType, Func3_5);
  and and_32 (bgeu, BType, Func3_7);
  and and_33 (blt, BType, Func3_4);
  not not_2 (not_2_out, BrLt);
  not not_3 (not_3_out, BrLt);
  and and_34 (sb, Stores, Func3_0);
  and and_35 (sh, Stores, Func3_1);
  and and_36 (sw, Stores, Func3_2);
  and and_37 (bltu, BType, Func3_6);
  and and_38 (bne, BType, Func3_1);
  // Priority_Encoder #(.select_enc(6)) priority_encoder_1: pin names not known; wires that end beside it: RomInput, add, mul, sub, sll0, mulh, mulhu, slt, xor0, srl0, sra0, or0, and0, lb, lh, lw, addi, slli, slti, xori, srli, srai, ori, andi, sb, sh, sw, beq, bne, blt, bge, bltu, bgeu, aiupc, lui, jal, jalr

  // Other names for the same wires on the sheet: Opcode[6:0] = Instruction[6:0]; Func3[2:0] = Instruction[14:12];
  //   Func7[6:0] = Instruction[31:25]

  // Notes on the sheet:
  //   INPUTS to your circuit
  //   This seperates the opcode/ funct 3/ and funct 7
  //   Do checks for which func3/func7 it is
  //   <-Signed
  //   <-unSigned
  //   contents of rom_1 (hex, n*v repeats v):
  //   100f 140f 160f 108f 148f 158f 110f 120f 128f 168f 130f 138f 41 41 41 1041 10c1 1141 1241 12c1 16c1
  //   1341 13c1 3842 3842 3842 4*3064 3074 3074 1067 17c7 2069 2041
  //   ROM FOR CONTROL LOGIC
  //   Function checks for RType
  //   DON'T CHANGE THE LOCATIONS OF THE INPUTS AND OUTPUTS!
  //   This is only if you choose to do the ROM option
  //   CONNECT
  //   WIRE
  //   TO
  //   USE
  //   ROM
  //   Function checks for Itype
  //   OUTPUT from your circuit
  //   Do checks for which type instruction the opcode is
  //   <-- 0 Extended
  //   <-- Sign Extended
  //   Function checks for I*type
  //   Function checks for Loads
  //   Reminder: If using ROM, use combinational logic for PCSel
  //   Basically do every single jump and branch check. If it jumps/branches then 1, otherwise 0.
  //   Function checks for Btype
  //   Function checks for Saves
  //   NOTE: I think this is supposed to be in the same order as the spreadsheet
  //   So I don't think it's a good idea to wire this up until we are done
  //   all of the possible commands are supposed to go in here
endmodule
