// Logisim project cpu.circ as structural Verilog: 1 circuit, main circuit cpu
module cpu (
  input  clk,
  input  [31:0] Instruction,
  input  [31:0] MemReadData,
  output [31:0] MemAddress,
  output [31:0] ProgramCounter,
  output [31:0] ra,
  output [31:0] sp,
  output [31:0] t0,
  output [31:0] t1,
  output [31:0] t2,
  output [31:0] s0,
  output [31:0] s1,
  output [31:0] a0,
  output [3:0] MemWriteMask,
  output [31:0] MemWriteData
);

  wire branch_comp_1_breq, branch_comp_1_brlt, control_logic_1_asel, control_logic_1_brun,
       control_logic_1_bsel, control_logic_1_memwen, control_logic_1_pcsel, control_logic_1_regwen;
  wire [1:0] control_logic_1_wbsel;
  wire [2:0] control_logic_1_immsel, funct3;
  wire [3:0] control_logic_1_alusel;
  wire [6:0] funct7;
  wire [24:0] Instruction1;
  wire [31:0] adder_1_out, Immediate, multiplexer_1_out, multiplexer_2_out, multiplexer_3_out,
       multiplexer_4_out, partial_load_1_datatoreg, PC4, ProgramCounter_t, ReadData1, ReadData2, WriteData;

  Adder #(.width(32)) adder_1 (.a(ProgramCounter), .b(32'h4), .out(adder_1_out));  // open: cin, cout
  Register #(.width(32)) PC (.D(multiplexer_1_out), .clk(clk), .Q(ProgramCounter));  // open: en, clr
  Multiplexer #(.width(32)) multiplexer_1 (
    .in0(adder_1_out), .in1(MemAddress), .out(multiplexer_1_out), .sel(control_logic_1_pcsel));
  Adder #(.width(32)) adder_2 (.a(ProgramCounter_t), .b(32'h4), .out(PC4));  // open: cin, cout
  Multiplexer #(.width(32)) multiplexer_2 (
    .in0(Instruction), .in1(32'h13), .out(multiplexer_2_out), .sel(control_logic_1_pcsel));
  Register #(.width(32)) register_1 (.D(ProgramCounter), .clk(clk), .Q(ProgramCounter_t));  // open: en, clr
  Register #(.width(32)) register_2 (
    .D(multiplexer_2_out), .clk(clk), .Q({funct7, Instruction1[24:15], funct3, Instruction1[11:0]}));  // open: en, clr
  control_logic control_logic_1 (
    .Instruction({funct7, Instruction1[24:15], funct3, Instruction1[11:0]}), .BrEq(branch_comp_1_breq),
    .BrLt(branch_comp_1_brlt), .PCSel(control_logic_1_pcsel), .RegWEn(control_logic_1_regwen),
    .ImmSel(control_logic_1_immsel), .BrUn(control_logic_1_brun), .ASel(control_logic_1_asel),
    .BSel(control_logic_1_bsel), .ALUSel(control_logic_1_alusel), .MemWEn(control_logic_1_memwen),
    .WBSel(control_logic_1_wbsel));
  regfile regfile_1 (
    .ReadIndex1(Instruction1[19:15]), .ReadIndex2(Instruction1[24:20]), .WriteIndex(Instruction1[11:7]),
    .WriteData(WriteData), .RegWEn(control_logic_1_regwen), .clk(clk), .ra(ra), .sp(sp), .t0(t0), .t1(t1),
    .t2(t2), .s0(s0), .s1(s1), .a0(a0), .ReadData1(ReadData1), .ReadData2(ReadData2));
  imm_gen imm_gen_1 (
    .Instruction({funct7, Instruction1[24:15], funct3, Instruction1[11:0]}), .ImmSel(control_logic_1_immsel),
    .Immediate(Immediate));
  Multiplexer #(.width(32)) multiplexer_3 (
    .in0(ReadData1), .in1(ProgramCounter_t), .out(multiplexer_3_out), .sel(control_logic_1_asel));
  Multiplexer #(.width(32)) multiplexer_4 (
    .in0(ReadData2), .in1(Immediate), .out(multiplexer_4_out), .sel(control_logic_1_bsel));
  alu alu_1 (.A(multiplexer_3_out), .B(multiplexer_4_out), .ALUSel(control_logic_1_alusel), .ALUResult(MemAddress));
  branch_comp branch_comp_1 (
    .BrData1(ReadData1), .BrData2(ReadData2), .BrUn(control_logic_1_brun), .BrEq(branch_comp_1_breq),
    .BrLt(branch_comp_1_brlt));
  partial_store partial_store_1 (
    .Instruction({funct7, Instruction1[24:15], funct3, Instruction1[11:0]}), .MemAddress(MemAddress),
    .DataFromReg(ReadData2), .MemWEn(control_logic_1_memwen), .MemWriteMask(MemWriteMask),
    .DataToMem(MemWriteData));
  partial_load partial_load_1 (
    .Instruction({funct7, Instruction1[24:15], funct3, Instruction1[11:0]}), .MemAddress(MemAddress),
    .DataFromMem(MemReadData), .DataToReg(partial_load_1_datatoreg));
  Multiplexer #(.select(2), .width(32)) multiplexer_5 (
    .in0(partial_load_1_datatoreg), .in1(MemAddress), .in2(PC4), .out(WriteData), .sel(control_logic_1_wbsel));  // open: in3

  // Other names for the same wires on the sheet: Opcode[6:0] = Instruction1[6:0]; rd[4:0] = Instruction1[11:7];
  //   Instruction1 (some bits) = {funct7, funct3}; rs1[4:0] = Instruction1[19:15]; rs2[4:0] = Instruction1[24:20];
  //   ProgramCounter1[31:0] = ProgramCounter; Result[31:0] = MemAddress

  // Notes on the sheet:
  //   Note: PCSel is 0 for PC + 4, and 1 for otherwise
  //   To IMEM
  //   IMEM (do **NOT** move this)
  //   From IMEM
  //   Inputs/Outputs for testing. Do **NOT** move these.
  //   Is this correct?->
  //   To DMEM
  //   DMEM (do **NOT** move this)
  //   From DMEM
endmodule
