// Logisim project partial-store.circ as structural Verilog: 1 circuit, main circuit partial_store
module partial_store (
  input  [31:0] Instruction,
  input  [31:0] MemAddress,
  input  [31:0] DataFromReg,
  input  MemWEn,
  output [3:0] MemWriteMask,
  output [31:0] DataToMem
);

  wire comparator_1_eq;
  wire [3:0] MemWriteMaskPossible, multiplexer_1_out, multiplexer_4_out;
  wire [31:0] bit_extender_1_out, bit_extender_2_out, multiplexer_3_out, multiplexer_5_out, shifter_1_out,
       shifter_2_out, shifter_3_out, shifter_4_out;

  assign bit_extender_1_out = {{16{1'b0}}, DataFromReg[15:0]};  // Bit_Extender bit_extender_1
  Comparator #(.width(7)) comparator_1 (.a(Instruction[6:0]), .b(7'b0100011), .eq(comparator_1_eq));  // open: gt, lt
  assign bit_extender_2_out = {{24{1'b0}}, DataFromReg[7:0]};  // Bit_Extender bit_extender_2
  Shifter #(.width(32)) shifter_1 (.in(bit_extender_1_out), .\dist (5'b10000), .out(shifter_1_out));
  Multiplexer #(.select(2), .width(4)) multiplexer_1 (
    .in0(4'b0011), .in2(4'b1100), .out(multiplexer_1_out), .sel(MemAddress[1:0]));  // open: in1, in3
  Multiplexer #(.width(4)) multiplexer_2 (
    .in0(4'b0000), .in1(MemWriteMaskPossible), .out(MemWriteMask), .sel(comparator_1_eq));
  Shifter #(.width(32)) shifter_2 (.in(bit_extender_2_out), .\dist (5'b01000), .out(shifter_2_out));
  Shifter #(.width(32)) shifter_3 (.in(bit_extender_2_out), .\dist (5'b10000), .out(shifter_3_out));
  Shifter #(.width(32)) shifter_4 (.in(bit_extender_2_out), .\dist (5'b11000), .out(shifter_4_out));
  Multiplexer #(.select(2), .width(32)) multiplexer_3 (
    .in0(bit_extender_1_out), .in2(shifter_1_out), .out(multiplexer_3_out), .sel(MemAddress[1:0]));  // open: in1, in3
  Multiplexer #(.select(2), .width(4)) multiplexer_4 (
    .in0(4'b0001), .in1(4'b0010), .in2(4'b0100), .in3(4'b1000), .out(multiplexer_4_out), .sel(MemAddress[1:0]));
  Multiplexer #(.select(2), .width(32)) multiplexer_5 (
    .in0(bit_extender_2_out), .in1(shifter_2_out), .in2(shifter_3_out), .in3(shifter_4_out),
    .out(multiplexer_5_out), .sel(MemAddress[1:0]));
  Multiplexer #(.select(2), .width(4)) multiplexer_6 (
    .in0(multiplexer_4_out), .in1(multiplexer_1_out), .in2(4'b1111), .out(MemWriteMaskPossible),
    .sel(Instruction[13:12]));  // open: in3
  Multiplexer #(.select(2), .width(32)) multiplexer_7 (
    .in0(multiplexer_5_out), .in1(multiplexer_3_out), .in2(DataFromReg), .out(DataToMem),
    .sel(Instruction[13:12]));  // open: in3

  // Notes on the sheet:
  //   INPUTS to your circuit
  //   DON'T CHANGE THE LOCATIONS OF THE INPUTS AND OUTPUTS!
  //   OUTPUT from your circuit
endmodule
