// Logisim project regfile.circ as structural Verilog: 1 circuit, main circuit regfile
module regfile (
  input  [4:0] ReadIndex1,
  input  [4:0] ReadIndex2,
  input  [4:0] WriteIndex,
  input  [31:0] WriteData,
  input  RegWEn,
  input  clk,
  output [31:0] ra,
  output [31:0] sp,
  output [31:0] t0,
  output [31:0] t1,
  output [31:0] t2,
  output [31:0] s0,
  output [31:0] s1,
  output [31:0] a0,
  output [31:0] ReadData1,
  output [31:0] ReadData2
);

  wire multiplexer_1_out, undriven, we0, we1, we2, we3, we4, we5, we6, we7, we8, we9, we10, we11, we12, we13,
       we14, we15, we16, we17, we18, we19, we20, we21, we22, we23, we24, we25, we26, we27, we28, we29, we30,
       we31;
  wire [31:0] Out0, Out3, Out4, Out11, Out12, Out13, Out14, Out15, Out16, Out17, Out18, Out19, Out20, Out21,
       Out22, Out23, Out24, Out25, Out26, Out27, Out28, Out29, Out30, Out31;

  Register #(.width(32)) Reg0 (.D({32{1'b0}}), .en(we0), .clk(clk), .Q(Out0));  // open: clr
  Register #(.width(32)) Reg4 (.D(WriteData), .en(we4), .clk(clk), .Q(Out4));  // open: clr
  Register #(.width(32)) Reg8 (.D(WriteData), .en(we8), .clk(clk), .Q(s0));  // open: clr
  Register #(.width(32)) Reg12 (.D(WriteData), .en(we12), .clk(clk), .Q(Out12));  // open: clr
  Register #(.width(32)) Reg16 (.D(WriteData), .en(we16), .clk(clk), .Q(Out16));  // open: clr
  Register #(.width(32)) Reg20 (.D(WriteData), .en(we20), .clk(clk), .Q(Out20));  // open: clr
  Register #(.width(32)) Reg24 (.D(WriteData), .en(we24), .clk(clk), .Q(Out24));  // open: clr
  Register #(.width(32)) Reg28 (.D(WriteData), .en(undriven), .clk(clk), .Q(Out28));  // open: clr
  Register #(.width(32)) Reg1 (.D(WriteData), .en(we1), .clk(clk), .Q(ra));  // open: clr
  Register #(.width(32)) Reg5 (.D(WriteData), .en(we5), .clk(clk), .Q(t0));  // open: clr
  Register #(.width(32)) Reg9 (.D(WriteData), .en(we9), .clk(clk), .Q(s1));  // open: clr
  Register #(.width(32)) Reg13 (.D(WriteData), .en(we13), .clk(clk), .Q(Out13));  // open: clr
  Register #(.width(32)) Reg17 (.D(WriteData), .en(we17), .clk(clk), .Q(Out17));  // open: clr
  Register #(.width(32)) Reg21 (.D(WriteData), .en(we21), .clk(clk), .Q(Out21));  // open: clr
  Register #(.width(32)) Reg25 (.D(WriteData), .en(we25), .clk(clk), .Q(Out25));  // open: clr
  Register #(.width(32)) Reg29 (.D(WriteData), .en(we29), .clk(clk), .Q(Out29));  // open: clr
  Multiplexer multiplexer_1 (.in0(1'b0), .in1(1'b1), .out(multiplexer_1_out), .sel(RegWEn));
  Demultiplexer #(.select(5)) demultiplexer_1 (
    .out0(we0), .out1(we1), .out2(we2), .out3(we3), .out4(we4), .out5(we5), .out6(we6), .out7(we7),
    .out8(we8), .out9(we9), .out10(we10), .out11(we11), .out12(we12), .out13(we13), .out14(we14),
    .out15(we15), .out16(we16), .out17(we17), .out18(we18), .out19(we19), .out20(we20), .out21(we21),
    .out22(we22), .out23(we23), .out24(we24), .out25(we25), .out26(we26), .out27(we27), .out28(we28),
    .out29(we29), .out30(we30), .out31(we31), .in(multiplexer_1_out), .sel(WriteIndex));
  Register #(.width(32)) Reg2 (.D(WriteData), .en(we2), .clk(clk), .Q(sp));  // open: clr
  Register #(.width(32)) Reg6 (.D(WriteData), .en(we6), .clk(clk), .Q(t1));  // open: clr
  Register #(.width(32)) Reg10 (.D(WriteData), .en(we10), .clk(clk), .Q(a0));  // open: clr
  Register #(.width(32)) Reg14 (.D(WriteData), .en(we14), .clk(clk), .Q(Out14));  // open: clr
  Register #(.width(32)) Reg18 (.D(WriteData), .en(we18), .clk(clk), .Q(Out18));  // open: clr
  Register #(.width(32)) Reg22 (.D(WriteData), .en(we22), .clk(clk), .Q(Out22));  // open: clr
  Register #(.width(32)) Reg26 (.D(WriteData), .en(we26), .clk(clk), .Q(Out26));  // open: clr
  Register #(.width(32)) Reg30 (.D(WriteData), .en(we30), .clk(clk), .Q(Out30));  // open: clr
  Register #(.width(32)) Reg3 (.D(WriteData), .en(we3), .clk(clk), .Q(Out3));  // open: clr
  Register #(.width(32)) Reg7 (.D(WriteData), .en(we7), .clk(clk), .Q(t2));  // open: clr
  Register #(.width(32)) Reg11 (.D(WriteData), .en(we11), .clk(clk), .Q(Out11));  // open: clr
  Register #(.width(32)) Reg15 (.D(WriteData), .en(we15), .clk(clk), .Q(Out15));  // open: clr
  Register #(.width(32)) Reg19 (.D(WriteData), .en(we19), .clk(clk), .Q(Out19));  // open: clr
  Register #(.width(32)) Reg23 (.D(WriteData), .en(we23), .clk(clk), .Q(Out23));  // open: clr
  Register #(.width(32)) Reg27 (.D(WriteData), .en(we27), .clk(clk), .Q(Out27));  // open: clr
  Register #(.width(32)) Reg31 (.D(WriteData), .en(we31), .clk(clk), .Q(Out31));  // open: clr
  Multiplexer #(.select(5), .width(32)) multiplexer_2 (
    .in0(Out0), .in1(ra), .in2(sp), .in3(Out3), .in4(Out4), .in5(t0), .in6(t1), .in7(t2), .in8(s0), .in9(s1),
    .in10(a0), .in11(Out11), .in12(Out12), .in13(Out13), .in14(Out14), .in15(Out15), .in16(Out16),
    .in17(Out17), .in18(Out18), .in19(Out19), .in20(Out20), .in21(Out21), .in22(Out22), .in23(Out23),
    .in24(Out24), .in25(Out25), .in26(Out26), .in27(Out27), .in28(Out28), .in29(Out29), .in30(Out30),
    .in31(Out31), .out(ReadData1), .sel(ReadIndex1));
  Multiplexer #(.select(5), .width(32)) multiplexer_3 (
    .in0(Out0), .in1(ra), .in2(sp), .in3(Out3), .in4(Out4), .in5(t0), .in6(t1), .in7(t2), .in8(s0), .in9(s1),
    .in10(a0), .in11(Out11), .in12(Out12), .in13(Out13), .in14(Out14), .in15(Out15), .in16(Out16),
    .in17(Out17), .in18(Out18), .in19(Out19), .in20(Out20), .in21(Out21), .in22(Out22), .in23(Out23),
    .in24(Out24), .in25(Out25), .in26(Out26), .in27(Out27), .in28(Out28), .in29(Out29), .in30(Out30),
    .in31(Out31), .out(ReadData2), .sel(ReadIndex2));

  // Notes on the sheet:
  //   INPUTS to your circuit
  //   DON'T CHANGE THE LOCATIONS OF THE INPUTS AND OUTPUTS!
  //   These are DEBUG/TEST outputs from your circuit.
  //   OUTPUTS from your circuit
endmodule
